// Digital circuit c.dig as structural Verilog
module c (
  input  in_2,
  input  in_3,
  input  in_4,
  input  in_5,
  output out_1
);

  wire or_1_out, or_2_out;

  or or_1 (or_1_out, in_2, in_3);
  or or_2 (or_2_out, in_4, in_5);
  and and_1 (out_1, or_1_out, or_2_out);
endmodule
