// Digital circuit e.dig as structural Verilog
module e (
  input  in_1,
  input  in_2,
  input  in_3,
  output out_4
);

  wire not_1_out, not_2_out;

  not not_1 (not_1_out, in_1);
  not not_2 (not_2_out, in_2);
  or or_1 (out_4, not_1_out, not_2_out, in_3);
endmodule
