// Digital circuit f.dig as structural Verilog
module f (
  input  in_1,
  input  in_2,
  input  in_3,
  input  in_5,
  output out_4
);

  wire and_1_out, nand_1_out;

  nand nand_1 (nand_1_out, in_1, in_2);
  and and_1 (and_1_out, in_3, in_5);
  nand nand_2 (out_4, nand_1_out, and_1_out);
endmodule
