// Digital circuit grindnat2.dig as structural Verilog
module grindnat2 (
  input  a,
  input  b,
  input  c,
  output y
);

  wire nor_1_out;

  nor nor_1 (nor_1_out, b, c);
  or or_1 (y, a, nor_1_out);
endmodule
