// Digital circuit grindnat3.dig as structural Verilog
module grindnat3 (
  input  a,
  input  b,
  input  c,
  input  d,
  output y
);

  wire and_1_out, and_2_out;

  and and_1 (and_1_out, a, b);
  and and_2 (and_2_out, c, d);
  xor xor_1 (y, and_1_out, and_2_out);
endmodule
