// Digital circuit grindnat4.dig as structural Verilog
module grindnat4 (
  input  a,
  input  b,
  input  c,
  output y
);

  wire and_1_out, not_1_out, not_2_out;

  not not_1 (not_1_out, a);
  not not_2 (not_2_out, b);
  and and_1 (and_1_out, not_1_out, not_2_out);
  or or_1 (y, and_1_out, c);
endmodule
